# Fritzing sketch Wiring (saved by Fritzing 1.0.0rc)
breadboards: 1

parts:
  Mod1 = Raspberry Pi Pico W
  DHT11_1 = DHT11 module
  Part4 = KY-019 5V Relay Module [package="Breakout board"]  # not connected
  Part5 = LCD1602-I2C

nets:
  N1: Mod1.pin_1, Part5.SDA
  N2: Mod1.pin_2, Part5.SCL
  GND: Mod1.pin_3, Mod1.pin_8, Mod1.pin_13, Mod1.pin_18, Mod1.pin_23, Mod1.pin_28, Mod1.pin_33, Mod1.pin_38, DHT11_1.GND, Part5.GND
  N3: Mod1.pin_21, DHT11_1.DATA
  N4: Mod1.pin_36, DHT11_1.VCC
  N5: Mod1.pin_40, Part5.VCC

notes:
  Relay is connected to power cable of desk fan
  Has I2C interface for LCD on the underside

custom parts:
  Raspberry Pi Pico W: Raspberry Pi Pico W. Based around the RP2040 microcontroller the Pico W is a low cost microcontroller device bringing Raspberry Pi quality, cost, and easy of use to the microcontroller space. The areas marked KEEPOUT in pcb silkscreen should not have traces running through them to avoid shorts on a soldered in module!
  DHT11 module: https://cdn-learn.adafruit.com/downloads/pdf/dht.pdf DHT11 black pcb module reference by:https://github.com/adafruit/Fritzing-Library/blob/master/parts/DHT11%20Humitidy%20and%20Temperature%20Sensor.fzpz
  KY-019 5V Relay Module: 5V Relay module KEYES KY-019, used to control AC circuits.
  LCD1602-I2C: A standard character display, usually with 2x16 characters. Comes in many colors with LCM1602 IIC attached.
